# Fritzing sketch Seismic_Activity_Detector (saved by Fritzing 0.9.3b)
circuit board: 6.77392cm x 5.45723cm
breadboards: 1

parts:
  Arduino = Arduino Nano (Rev3.0) (ICSP)
  ADXL345 = Triple Axis Accelerometer Breakout - ADXL345
  J1 = Piezo Speaker
  R1 = Resistor [tolerance=±5% resistance=220 package=THT]
  LED1 = smd LED [color="Red (633nm)" package="0603 [SMD]"]

nets:
  GND: Arduino.GND, ADXL345.GND, J1.pin2, LED1.cathode
  N1: Arduino.D12/MISO, J1.pin1
  5V: Arduino.5V, ADXL345.VCC
  N2: Arduino.A5, ADXL345.SCL
  N3: Arduino.A4, ADXL345.SDA
  N4: Arduino.D13/SCK, R1.Pin_0
  N5: R1.Pin_1, LED1.anode
